# Fritzing sketch nano_gy80_wiring_HORIZONTALLY_INVERTED (saved by Fritzing 0.8.5b)

parts:
  Bauteil1 = Arduino Nano (Rev3.0)
  GY1 = GY-80

nets:
  GND: Bauteil1.GND, GY1.GND
  N1: Bauteil1.5V, GY1.VCC_IN
  N2: Bauteil1.A5, GY1.SCL
  N3: Bauteil1.A4, GY1.SDA

custom parts:
  GY-80: Placa GY-80 basada en conjunto de giroscopios L3G4200D + acelerómetros ADXL345 + magnetómetro HMC5883L + sensor barométrico BMP085
